# Fritzing sketch WeMos-D1 (saved by Fritzing 0.9.3b)
breadboards: 1

parts:
  WeMos_D1_Mini1 = WeMos D1 Mini
  RHT1 = Humidity and Temperature Sensor RHT03

nets:
  3V3: WeMos_D1_Mini1.3V3, RHT1.Vcc
  N1: WeMos_D1_Mini1.D1, RHT1.Data-signal
  N2: WeMos_D1_Mini1.G, RHT1.GND_2
