# Fritzing sketch Project Part-2 (saved by Fritzing 0.9.3b)
breadboards: 1

parts:
  Raspberry_Pi_1 = Raspberry Pi 3 [part_number=RPI-3-V1.2]
  LED1 = LEDs [package=led10mm]

nets:
  N1: Raspberry_Pi_1.GIPO18, LED1.A
  N2: Raspberry_Pi_1.GND, LED1.C
